// Logisim project TallerLogica-Combinatorios.circ as structural Verilog: 9 circuits, main circuit sumador_simple
module sumador_simple (
  input  A,
  input  B,
  output S,
  output Cout
);

  xor xor_1 (S, A, B);
  and and_1 (Cout, A, B);
endmodule

module sumador_completo (
  input  Cin,
  input  A,
  input  B,
  output S,
  output Cout
);

  wire sumador_simple_1_cout, sumador_simple_1_s, sumador_simple_2_cout;

  sumador_simple sumador_simple_1 (.A(A), .B(B), .S(sumador_simple_1_s), .Cout(sumador_simple_1_cout));
  sumador_simple sumador_simple_2 (.A(Cin), .B(sumador_simple_1_s), .S(S), .Cout(sumador_simple_2_cout));
  or or_1 (Cout, sumador_simple_2_cout, sumador_simple_1_cout);
endmodule

module sumador_4 (
  input  Cin,
  input  [3:0] A,
  input  [3:0] B,
  output [3:0] S,
  output Cout
);

  wire sumador_completo_1_cout, sumador_completo_2_cout, sumador_completo_3_cout;

  sumador_completo sumador_completo_1 (.Cin(Cin), .A(A[0]), .B(B[0]), .S(S[0]), .Cout(sumador_completo_1_cout));
  sumador_completo sumador_completo_2 (
    .Cin(sumador_completo_1_cout), .A(A[1]), .B(B[1]), .S(S[1]), .Cout(sumador_completo_2_cout));
  sumador_completo sumador_completo_3 (
    .Cin(sumador_completo_2_cout), .A(A[2]), .B(B[2]), .S(S[2]), .Cout(sumador_completo_3_cout));
  sumador_completo sumador_completo_4 (.Cin(sumador_completo_3_cout), .A(A[3]), .B(B[3]), .S(S[3]), .Cout(Cout));
  Hex_Digit_Display hex_digit_display_1 (.value(S));  // open: dp
endmodule

module comparador_cero (
  input  [3:0] A,
  output Z
);

  wire or_1_out, or_2_out, or_3_out;

  or or_1 (or_1_out, A[0], A[1]);
  or or_2 (or_2_out, A[2], A[3]);
  or or_3 (or_3_out, or_1_out, or_2_out);
  not not_1 (Z, or_3_out);
endmodule

module sumador_flags (
  input  Cin,
  input  [3:0] A,
  input  [3:0] B,
  output [3:0] S,
  output Z,
  output C,
  output N,
  output V
);

  wire not_1_out, xor_1_out, xor_2_out;

  xor xor_1 (xor_1_out, A[3], B[3]);
  not not_1 (not_1_out, xor_1_out);
  Hex_Digit_Display hex_digit_display_1 (.value({N, S[2:0]}));  // open: dp
  sumador_4 sumador_4_1 (.Cin(Cin), .A(A), .B(B), .S({N, S[2:0]}), .Cout(C));
  xor xor_2 (xor_2_out, N, not_1_out);
  and and_1 (V, xor_2_out, not_1_out);
  comparador_cero comparador_cero_1 (.A({N, S[2:0]}), .Z(Z));

  assign S[3] = N;
endmodule

module incrementador_4 (
  input  [3:0] A,
  output [3:0] S
);

  sumador_4 sumador_4_1 (.Cin(1'b1), .A(A), .B(4'b0000), .S(S));  // open: Cout
  Hex_Digit_Display hex_digit_display_1 (.value(S));  // open: dp
endmodule

module inversor_4 (
  input  [3:0] A,
  input  INV,
  output [3:0] S
);

  wire [3:0] incrementador_4_1_s, not_1_out;

  not not_1 (not_1_out[0], A[0]);
  not not_2 (not_1_out[1], A[1]);
  not not_3 (not_1_out[2], A[2]);
  not not_4 (not_1_out[3], A[3]);
  Multiplexer #(.width(4)) multiplexer_1 (.in0(A), .in1(incrementador_4_1_s), .out(S), .sel(INV));
  incrementador_4 incrementador_4_1 (.A(not_1_out), .S(incrementador_4_1_s));
  Hex_Digit_Display hex_digit_display_1 (.value(S));  // open: dp
endmodule

module ALU (
  input  [3:0] A,
  input  [3:0] B,
  input  [1:0] OP,
  output C,
  output V,
  output Z,
  output N,
  output [3:0] S
);

  wire and_5_out, comparador_cero_1_z, multiplexer_2_out, multiplexer_3_out, not_1_out, not_2_out,
       sumador_flags_1_c, sumador_flags_1_v;
  wire [3:0] and_1_out, inversor_4_1_s, or_1_out, sumador_flags_1_s;

  inversor_4 inversor_4_1 (.A(B), .INV(multiplexer_2_out), .S(inversor_4_1_s));
  and and_1 (and_1_out[0], B[0], A[0]);
  and and_2 (and_1_out[1], B[1], A[1]);
  and and_3 (and_1_out[2], B[2], A[2]);
  and and_4 (and_1_out[3], B[3], A[3]);
  or or_1 (or_1_out[0], A[0], B[0]);
  or or_2 (or_1_out[1], A[1], B[1]);
  or or_3 (or_1_out[2], A[2], B[2]);
  sumador_flags sumador_flags_1 (
    .Cin(1'b0), .A(A), .B(inversor_4_1_s), .S(sumador_flags_1_s), .Z(Z), .C(sumador_flags_1_c), .N(N),
    .V(sumador_flags_1_v));
  or or_4 (or_1_out[3], A[3], B[3]);
  Multiplexer #(.select(2), .width(4)) multiplexer_1 (
    .in0(sumador_flags_1_s), .in1(sumador_flags_1_s), .in2(and_1_out), .in3(or_1_out), .out(S), .sel(OP));
  not not_1 (not_1_out, sumador_flags_1_c);
  comparador_cero comparador_cero_1 (.A(sumador_flags_1_s), .Z(comparador_cero_1_z));
  Multiplexer #(.select(2)) multiplexer_2 (
    .in0(1'b0), .in1(1'b1), .in2(1'b0), .in3(1'b0), .out(multiplexer_2_out), .sel(OP));
  and and_5 (and_5_out, not_1_out, not_2_out);
  not not_2 (not_2_out, comparador_cero_1_z);
  Hex_Digit_Display hex_digit_display_1 (.value(S));  // open: dp
  Multiplexer #(.select(2)) multiplexer_3 (
    .in0(sumador_flags_1_c), .in1(and_5_out), .in2(1'b0), .in3(1'b0), .out(multiplexer_3_out), .sel(OP));
  Multiplexer #(.select(2)) multiplexer_4 (
    .in0(multiplexer_3_out), .in1(multiplexer_3_out), .in2(1'b0), .in3(1'b0), .out(C), .sel(OP));
  Multiplexer #(.select(2)) multiplexer_5 (
    .in0(sumador_flags_1_v), .in1(sumador_flags_1_v), .in2(1'b0), .in3(1'b0), .out(V), .sel(OP));

  // Notes on the sheet:
  //   Cuidado con el - -8 arreglar
endmodule

module verificador (
  output [3:0] out_1,
  output [3:0] out_2,
  output [1:0] out_3,
  output halt,
  output N,
  output Z,
  output V,
  output C,
  output [3:0] res
);

  wire clock_1_out;

  Clock clock_1 (.out(clock_1_out));
  Counter #(.max('h3ff), .width(10)) counter_1 (
    .clk(clock_1_out), .carry(halt), .Q({out_3, out_2, out_1}));  // open: clr, load, up, count, D
  ALU alu_1 (.A(out_1), .B(out_2), .OP(out_3), .C(N), .V(Z), .Z(V), .N(C), .S(res));
endmodule
